# Fritzing sketch dispenser-1 (saved by Fritzing 0.9.3b)
circuit board: 8.46667cm x 5.64444cm
breadboards: 2

parts:
  J1 = Basic Servo
  ESP32-30pin1 = esp32
  VCC1 = Battery block 9V
  U3 = Voltage Regulator - 3.3V [package="TO220 [THT]"]
  U4 = Voltage Regulator - 5V [package="TO220 [THT]"]
  C2 = Electrolytic Capacitor [capacitance=4.7mF voltage=35V part_number=6000 package="300 mil [THT, electrolytic]"]
  C3 = Electrolytic Capacitor [capacitance=4.7mF voltage=35V part_number=6000 package="300 mil [THT, electrolytic]"]

nets:
  GND: J1.gnd, ESP32-30pin1.gnd, ESP32-30pin1.GND, VCC1.-, U3.GND, U4.GND, C2.-, C3.-
  N1: J1.vcc, U4.output_voltage, C2.+, C3.+
  N2: J1.pulse, ESP32-30pin1.d19
  N3: ESP32-30pin1.3V3, U3.output_voltage
  N4: VCC1.+, U3.input_voltage, U4.input_voltage

custom parts:
  esp32: based on work of Roman Minyaylov, at https://github.com/roman-minyaylov/nodemcu-v3-fritzing
