# Fritzing sketch servo-controller-schema (saved by Fritzing 0.9.3b)
breadboards: 2

parts:
  Power_plug1 = Power plug
  ESP32-30pin1 = esp32
  U1 = Voltage Regulator - 3.3V [package="TO220 [THT]"]
  Q1 = npn-Powertransistor [package="TO220 [THT]"]
  R1 = Resistor [tolerance=±5% resistance=220 package="0805 [SMD]"]
  R2 = Rotary Potentiometer (Large) [maximum_resistance=100kΩ package=THT]
  R3 = Resistor [tolerance=±5% resistance=2.2k package=THT]
  J1 = Basic Servo

nets:
  GND: Power_plug1.GND, ESP32-30pin1.d18, ESP32-30pin1.gnd, ESP32-30pin1.GND, ESP32-30pin1.d27, U1.GND, R1.Pin_1, R2.leg1, J1.gnd
  VCC: Power_plug1.VCC, U1.input_voltage, J1.vcc
  N1: ESP32-30pin1.d19, ESP32-30pin1.3V3, ESP32-30pin1.d14, Q1.base, R3.Pin_0, J1.pulse
  N2: ESP32-30pin1.d32, R1.Pin_0, R2.wiper
  N3: U1.output_voltage, Q1.collector
  N4: R2.leg2, R3.Pin_1

custom parts:
  esp32: based on work of Roman Minyaylov, at https://github.com/roman-minyaylov/nodemcu-v3-fritzing
